# Fritzing sketch SmartRoomController (saved by Fritzing 1.0.2b)
circuit board: 8.46667cm x 5.64444cm
breadboards: 3

parts:
  Breadboard4 = Breadboard Split Power
  Breadboard5 = Breadboard Split Power
  A1 = Particle - Photon2
  Part2 = NeoPixel Stick [part_number=1426]
  OLED_I2C1 = OLED 128x64 I2C Monochrome Display
  R1 = Resistor [tolerance=±5% power=0.25W resistance=10k package=THT]
  R2 = Resistor [tolerance=±5% power=0.25W resistance=10k package=THT]
  R3 = Resistor [tolerance=±5% power=0.25W resistance=10k package=THT]
  S1 = Pushbutton [package="[THT]"]
  S2 = Pushbutton [package="[THT]"]
  S3 = Pushbutton [package="[THT]"]
  Part3 = KY-003 Hall Magnetic Sensor Module [package="Breakout board"]
  US-1 = US-016
  PIR1 = PIR sensor
  R4 = Resistor [tolerance=±5% power=0.25W resistance=10000 package=THT]

nets:
  GND: Breadboard4.pin3Z, Breadboard4.pin20Z, Breadboard4.pin29Z, Breadboard5.pin3Z, Breadboard5.pin28Z, A1.Pin_4, A1.Pin_30, A1.Pin_35, OLED_I2C1.GND, R1.Pin_1, R2.Pin_1, R3.Pin_1, US-1.GND, PIR1.GND, R4.Pin_0
  VDD: Breadboard4.pin5Y, Breadboard4.pin15Y, Breadboard4.pin17Y, Breadboard4.pin22Y, Breadboard4.pin29Y, Breadboard5.pin3Y, Breadboard5.pin15Y, Breadboard5.pin17Y, Breadboard5.pin29Y, A1.Pin_2, A1.Pin_31, OLED_I2C1.VDD, S1.Pin_1, S1.Pin_2, S2.Pin_1, S2.Pin_2, S3.Pin_1, S3.Pin_2, US-1.VCC, PIR1.VDD
  N1: A1.Pin_5, US-1.Out
  N2: A1.Pin_6, US-1.Range
  N3: A1.Pin_10, R2.Pin_0, S1.Pin_3, S1.Pin_4
  N4: A1.Pin_11, R3.Pin_0, S2.Pin_3, S2.Pin_4
  N5: A1.Pin_12, R1.Pin_0, S3.Pin_3, S3.Pin_4
  N6: A1.Pin_17, OLED_I2C1.SDA
  N7: A1.Pin_18, OLED_I2C1.SCK
  N8: A1.Pin_19, Part2.DATAIN
  N9: A1.Pin_23, A1.Pin_37, PIR1.SIG, R4.Pin_1
  N10: A1.Pin_24, Part3.S
  +5V: A1.Pin_26, Part2.+5V, Part3.Vin
  N11: Part2.GND, Part3.-

custom parts:
  Breadboard Split Power: A custom 6 pin per group power supply strip where the top row (ground) is all bussed together and the bottom row (+V) is split in two groups of 12 pins. This version is modified to be a loadable part and was rescaled to be on the standard 1px = 1thou grid with the size set in inches
  Particle - Photon2: The Photon 2 is a microcontroller and Wi-Fi networking developed by particle. Features: 802.11a/b/g/n Wi-Fi, 2.4 GHz and 5 GHz Integrated PCB antenna Integrated U.FL connector for external antenna Integrated RF switch BLE 5 using same antenna as Wi-Fi Realtek RTL8721DM MCU ARM Cortex M33 CPU, 200 MHz 2048 KB (2 MB) user application maximum size 3072 KB (3 MB) of RAM available to user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
  NeoPixel Stick: Make your own little LED strip arrangement with this stick of NeoPixel LEDs. We crammed 8 of the tiny 5050 (5mm x 5mm) smart RGB LEDs onto a PCB with mounting holes and a chainable design. Use only one microcontroller pin to control as many as you can chain together! Each LED is addressable as the driver chip is inside the LED. Each one has ~18mA constant current drive so the color will be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
  Pushbutton: A generic pushbutton.
  KY-003 Hall Magnetic Sensor Module: KEYES KY-003 Arduino Hall Magnetic Sensor Module is a switch that will turn on/off in the presence of a magnetic field.
  US-016: This is a US-016 Distance Sensor with analog output capabilities
